# Fritzing sketch tank-schematic (saved by Fritzing 1.0.4)

parts:
  Part1 = Arduino Mega 2560 (Rev3)
  HC-SR04 = HC-SR04 Ultrasonic Distance Sensor
  TB6612FNG = Motor Driver 1A Dual TB6612FNG
  HMC5883L = Triple Axis Magnetometer - HMC5883 Breakout
  Rear_LED = LED - 3mm [color="Red (633nm)" current=0.030A package="3 mm [THT]"]
  Front_LED = LED - 3mm [color="White (4500K)" current=0.030A package="3 mm [THT]"]
  Bluetooth_LED = LED - 3mm [color="Blue (430nm)" current=0.030A package="3 mm [THT]"]
  Status_LED = LED - 3mm [color="Green (560nm)" current=0.030A package="3 mm [THT]"]
  SHT-40 = Adafruit SHT4x [part_number="Adafruit #4885"]
  Bluetooth_HM-10 = Bluetooth HM-10
  M1 = DC Motor [voltage_(max)=6V voltage_(min)=3V]
  part = Resistor [tolerance=±5% resistance=1k package="2512 [SMD]"]
  part_2 = Resistor [tolerance=±5% resistance=2k package="2512 [SMD]"]
  part_3 = Resistor [tolerance=±5% resistance=220 package="2512 [SMD]"]
  M2 = DC Motor [voltage_(max)=6V voltage_(min)=3V]
  VCC_(connected_directly_to_the_motors_board_and_Arduino) = 4 x AAA Battery Mount [internal_resistance=0.1Ω]
  R2 = Resistor [tolerance=±5% resistance=330 package="2512 [SMD]"]
  R9 = Resistor [tolerance=±5% resistance=330 package="2512 [SMD]"]
  3x = Resistor [tolerance=±5% resistance=330 package="2512 [SMD]"]

nets:
  N1: Part1.D21/SCL, Part1.SCL, HMC5883L.SCL, SHT-40.SCL
  N2: Part1.D20/SDA, Part1.SDA, HMC5883L.SDA, SHT-40.SDA
  N3: Part1.D13_PWM, part.Pin_0
  N4: Part1.D12_PWM, Bluetooth_HM-10.TXD
  N5: Part1.D8_PWM, TB6612FNG.STBY
  3V3: Part1.3V3, SHT-40.3.3V, Bluetooth_HM-10.VCC
  VCC: Part1.5V, HC-SR04.VCC, TB6612FNG.VCC, HMC5883L.VCC
  GND: Part1.GND, HC-SR04.GND, TB6612FNG.GND, HMC5883L.GND, Rear_LED.cathode, Front_LED.cathode, Bluetooth_LED.cathode, Status_LED.cathode, SHT-40.GND, Bluetooth_HM-10.GND, part_2.Pin_1
  N6: Part1.D2_PWM, TB6612FNG.AIN1
  N7: Part1.D3_PWM, TB6612FNG.AIN2
  N8: Part1.D4_PWM, TB6612FNG.PWMA
  N9: Part1.D5_PWM, TB6612FNG.BIN2
  N10: Part1.D6_PWM, TB6612FNG.BIN1
  N11: Part1.D7_PWM, TB6612FNG.PWMB
  N12: Part1.D30, HC-SR04.ECHO
  N13: Part1.D32, HC-SR04.TRIG
  N14: Part1.D48, R9.Pin_1
  N15: Part1.D50, 3x.Pin_1
  N16: Part1.D52, R2.Pin_1
  N17: TB6612FNG.B01, M2.pin_1
  N18: TB6612FNG.B02, M2.pin_2
  N19: TB6612FNG.A02, M1.pin_2
  N20: TB6612FNG.A01, M1.pin_1
  N21: TB6612FNG.VM, VCC_(connected_directly_to_the_motors_board_and_Arduino).+
  N22: Rear_LED.anode, R9.Pin_0
  N23: Front_LED.anode, 3x.Pin_0
  N24: Bluetooth_LED.anode, part_3.Pin_1
  N25: Status_LED.anode, R2.Pin_0
  N26: Bluetooth_HM-10.STATE, part_3.Pin_0
  N27: part.Pin_1, part_2.Pin_0

custom parts:
  Adafruit SHT4x: Sensirion Temperature/Humidity sensors are some of the finest & highest-accuracy devices you can get. And finally, we have some that have a true I2C interface for easy reading. The SHT40 and SHT45 sensors are the fourth generation (started at the SHT10 and worked its way up to the top!). The SHT40 has an excellent ±1.8% typical relative humidity accuracy from 25 to 75% and ±0.2 °C typical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
